# Fritzing sketch frankenNabaz_wiring (saved by Fritzing 0.9.3b)
circuit board: 8.46667cm x 5.64444cm
breadboards: 1

parts:
  Composant1 = Arduino Nano (Rev3.0)
  JP1 = Header 6 [package=molex-1x6_lock]
  JP2 = Header 6 [package=molex-1x6_lock]
  R1 = Resistor [tolerance=±5% resistance=220 package=THT]
  R2 = Resistor [tolerance=±5% resistance=10k package=THT]
  R3 = Resistor [tolerance=±5% resistance=220 package=THT]
  R4 = Resistor [tolerance=±5% resistance=10k package=THT]
  JP5 = Header 6 [package=molex-1x6_lock]
  JP6 = Header 2 [package=jst-2-smd-vert]
  JP7 = Header 2 [package=jst-2-smd-vert]
  Disp1 = LBT2088AH [part_number=LBT2088AH]  # not connected
  JP10 = Header 6 [package=molex-1x6-ra]
  R5 = Rotary Potentiometer (Large) [maximum_resistance=100kΩ package=THT]
  S1 = Round Pushbutton
  LED1 = RGB LED (com. anode, rbg) [package="5 mm [THT]"]
  LED2 = RGB LED (com. anode, rbg) [package="5 mm [THT]"]

nets:
  N1: Composant1.GND, JP1.2, JP2.2, R2.Pin_1, R4.Pin_1, R5.leg1, S1.leg0
  N2: Composant1.D3, LED1.green_cathode
  N3: Composant1.D4, LED1.blue_cathode
  N4: Composant1.D5, LED1.red_cathode
  N5: Composant1.D6, JP5.3
  N6: Composant1.D7, JP5.4
  N7: Composant1.D8, JP5.5
  N8: Composant1.D9, JP5.6
  N9: Composant1.D10, JP10.5
  N10: Composant1.D11/MOSI, JP10.4
  N11: Composant1.D12/MISO, JP10.3
  N12: Composant1.5V, R1.Pin_0, R3.Pin_0, R5.leg2, LED2.common_anode
  N13: Composant1.A7, LED2.red_cathode
  N14: Composant1.A6, LED2.blue_cathode
  N15: Composant1.A5, LED2.green_cathode
  N16: Composant1.A3, S1.leg1
  N17: Composant1.A2, R5.wiper
  N18: Composant1.A1, JP2.4, R4.Pin_0
  N19: Composant1.A0, JP1.4, R2.Pin_0
  N20: Composant1.3V3, JP1.3, JP2.3
  N21: JP1.1, R1.Pin_1
  N22: JP1.5, JP7.2
  N23: JP1.6, JP7.1
  N24: JP2.1, R3.Pin_1
  N25: JP2.5, JP6.2
  N26: JP2.6, JP6.1
  N27: JP5.1, JP10.1
  N28: JP5.2, JP10.2, LED1.common_anode

notes:
  right ear
  left ear
  scroll wheel
  right cheek
  head button
  left cheek
  mouth
  L9110 driver

custom parts:
  Header 6: Header 6 Standard 6-pin 0.1 header. Use with straight break away headers (SKU : PRT-00116), right angle break away headers (PRT-00553), swiss pins (PRT-00743), machine pins (PRT-00117), and female headers (PRT-00115). Molex polarized connector foot print use with SKU : PRT-08094 with associated crimp pins and housings. NOTES ON THE VARIANTS LOCK and LOCK_LONGPADS... This footprint was designed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
